# Fritzing sketch CONEXÃO DO CARRINHO RC (saved by Fritzing 1.0.4)
breadboards: 1

parts:
  M1 = DOIT Esp32 DevKit v1 (30 pins long, 11 pins width) [part_number=ESP32S-PIN30]
  L298N1 = L298N DC motor driver
  L298N2 = L298N DC motor driver
  HC-SR04_Sensor_1 = HC-SR04 Ultrasonic Distance Sensor
  J1 = Piezo Speaker
  BAT1 = Battery Holders [package=lipo-1100mAh]
  M2 = DC Motor [voltage_(max)=6V voltage_(min)=3V]  # not connected
  M4 = DC Motor [voltage_(max)=6V voltage_(min)=3V]  # not connected
  M5 = DC Motor [voltage_(max)=6V voltage_(min)=3V]  # not connected
  M6 = DC Motor [voltage_(max)=6V voltage_(min)=3V]  # not connected
  R1 = Resistor [tolerance=±5% power=0.25W resistance=1k package=THT]
  R2 = Resistor [tolerance=±5% power=0.25W resistance=2k package=THT]

nets:
  GND: M1.GND, HC-SR04_Sensor_1.GND, J1.pin1, BAT1.-, R2.Pin_1
  N1: M1.D4, HC-SR04_Sensor_1.TRIG
  N2: M1.RX2, L298N1.IN4
  N3: M1.TX2, L298N1.ENB
  N4: M1.D18, L298N1.IN3
  N5: M1.D19, L298N1.IN2
  N6: M1.D22, L298N1.IN1
  N7: M1.D35, R1.Pin_1
  N8: M1.D32, L298N1.ENA
  N9: M1.D33, L298N2.ENB
  N10: M1.D25, L298N2.IN4
  N11: M1.D26, L298N2.IN3
  N12: M1.D27, L298N2.IN2
  N13: M1.D14, L298N2.IN1
  N14: M1.D13, L298N2.ENA
  VIN: M1.VIN, L298N2.5V, HC-SR04_Sensor_1.VCC
  12V: L298N1.12V, L298N2.12V, BAT1.+
  GND_2: L298N1.GND, L298N2.GND
  N15: HC-SR04_Sensor_1.ECHO, R1.Pin_0

custom parts:
  DOIT Esp32 DevKit v1 (30 pins long, 11 pins width): The DOIT Esp32 DevKit v1 is one of the development board created by DOIT to evaluate the ESP-WROOM-32 module. It is based on the ESP32 microcontroller that boasts Wifi, Bluetooth, Ethernet and Low Power support all in a single chip. (vanepp) made breadboard work, adjusted pin numbering and labels and reduced size of schematic and cleaned up pcb. This chip is 30pins long (2 x15) and 11 pins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
  L298N DC motor driver: 2x DC motor driver with 78M05 positive voltage regulator (7..35 V) L298N: max 46 V, 2 A Set 5 V Enable jumper to enable 5 V regultor (needed for the L298N) and +5 V output at screw terminal or supply external +5 V at screw terminal Set ENA and/or ENB to +5 V to enable motor permanently or supply ENA and/or ENB with PWM signal IN1 and IN2 set rotation directory for motor A (OUT1/OUT2) IN2 and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
